# Fritzing sketch Stripboard (saved by Fritzing 0.8.3b)
stripboards: 2

parts:
  IC1 = IC, DIP package, 14 pins [chip_label=ATTiny44]
  VCC1 = Battery
  R1 = Resistor [tolerance=±5% resistance=1M package=THT]

nets:
  N1: IC1.pin1, VCC1.+
  N2: IC1.pin5, R1.Pin_1
  N3: IC1.pin6, R1.Pin_0
  N4: IC1.pin14, VCC1.-

notes:
  Display Horizonal
  Display Center
  Display Diagonal 2
  Display Diagonal 1
  Touch +
  Display Ground
  Touch -
  Cut traces under IC
